# Fritzing sketch diagram (saved by Fritzing 0.8.7b)
breadboards: 1

parts:
  U1 = DRV8833
  Part1 = Arduino Uno (Rev3) - ICSP
  J1 = Basic Servo
  PING)))_SENSOR1 = PING))) SENSOR
  LED1 = LED - 5mm [color="Red (633nm)" package="5 mm [THT]"]
  M1 = DC Motor
  M2 = DC Motor
  BAT1 = BC9VPC [package=bc9vpc]

nets (from the schematic view):
  GND: U1.GND, Part1.GND, J1.gnd, PING)))_SENSOR1.GND, LED1.cathode, BAT1.V-
  N1: U1.BIN1, Part1.D10_PWM/SS
  N2: U1.BIN2, Part1.D9_PWM
  N3: U1.AIN2, Part1.D5_PWM
  N4: U1.AIN1, Part1.D6_PWM
  VIN: U1.VIN, Part1.VIN, BAT1.V+
  N5: U1.BOUT1, M2.pin_1
  N6: U1.BOUT2, M2.pin_2
  N7: U1.AOUT2, M1.pin_2
  N8: U1.AOUT1, M1.pin_1
  N9: Part1.D13/SCK, LED1.anode
  N10: Part1.D2, J1.pulse
  5V: Part1.D4, Part1.5V, J1.vcc, PING)))_SENSOR1.5V, PING)))_SENSOR1.SIGNAL

custom parts:
  DRV8833: The DRV8833 provides a dual bridge motor driver solution for toys, printers, and other mechatronic applications.
